# Fritzing sketch 03_passiveBuzzer (saved by Fritzing 0.9.2b)
breadboards: 1

parts:
  Raspberry_Pi1 = Raspberry Pi 2
  R1 = Resistor [tolerance=±5% resistance=1k package="2512 [SMD]"]
  Q1 = PNP-Transistor [package="TO92 [THT]"]
  J1 = Piezo Speaker

nets:
  N1: Raspberry_Pi1.3v3, J1.pin2
  N2: Raspberry_Pi1.GPIO18, R1.Pin_1
  N3: Raspberry_Pi1.GND, Q1.C
  N4: R1.Pin_0, Q1.B
  N5: Q1.E, J1.pin1
