# Fritzing sketch 04_tiltSwitch (saved by Fritzing 0.9.2b)
breadboards: 1

parts:
  Raspberry_Pi1 = Raspberry Pi 2
  R1 = Resistor [tolerance=±5% resistance=220 package="2512 [SMD]"]
  LED1 = smd LED [color="Red (633nm)" package="0603 [SMD]"]
  S1 = Tilt Switch [package=THT]

nets:
  N1: Raspberry_Pi1.3v3, R1.Pin_1
  N2: Raspberry_Pi1.GPIO17, LED1.cathode
  N3: Raspberry_Pi1.GND, S1.Pin_2
  N4: Raspberry_Pi1.GPIO18, S1.Pin_1
  N5: R1.Pin_0, LED1.anode
