# Fritzing sketch 06_relay (saved by Fritzing 0.9.2b)
breadboards: 1

parts:
  Raspberry_Pi1 = Raspberry Pi 2
  R1 = Resistor [tolerance=±5% resistance=1k package="2512 [SMD]"]
  K1 = Relay [part_number=FRS1B-S package=THT]
  D1 = Rectifier Diode [part_number=1N4001 package="Melf DO-213 AB [SMD]"]
  Q2 = TRANSISTOR_NPN [package=to-92]

nets:
  N1: Raspberry_Pi1.GPIO18, R1.Pin_1
  N2: Raspberry_Pi1.GND, Q2.E
  N3: Raspberry_Pi1.5V, K1.COIL2, D1.cathode
  N4: R1.Pin_0, Q2.B
  N5: K1.COIL1, D1.anode, Q2.C
  N6: K1.C1, K1.C2
