# Fritzing sketch 07_flowingLed (saved by Fritzing 0.9.2b)
breadboards: 1

parts:
  Raspberry_Pi1 = Raspberry Pi 2
  R1 = Resistor [tolerance=±5% resistance=220 package="2512 [SMD]"]
  LED1 = smd LED [color="Red (633nm)" package="0603 [SMD]"]
  LED2 = smd LED [color="Red (633nm)" package="0603 [SMD]"]
  LED3 = smd LED [color="Red (633nm)" package="0603 [SMD]"]
  LED4 = smd LED [color="Red (633nm)" package="0603 [SMD]"]
  LED5 = smd LED [color="Red (633nm)" package="0603 [SMD]"]
  LED6 = smd LED [color="Red (633nm)" package="0603 [SMD]"]
  LED7 = smd LED [color="Red (633nm)" package="0603 [SMD]"]
  LED8 = smd LED [color="Red (633nm)" package="0603 [SMD]"]
  R2 = Resistor [tolerance=±5% resistance=220 package="2512 [SMD]"]
  R3 = Resistor [tolerance=±5% resistance=220 package="2512 [SMD]"]
  R4 = Resistor [tolerance=±5% resistance=220 package="2512 [SMD]"]
  R5 = Resistor [tolerance=±5% resistance=220 package="2512 [SMD]"]
  R6 = Resistor [tolerance=±5% resistance=220 package="2512 [SMD]"]
  R7 = Resistor [tolerance=±5% resistance=220 package="2512 [SMD]"]
  R8 = Resistor [tolerance=±5% resistance=220 package="2512 [SMD]"]

nets:
  N1: Raspberry_Pi1.3v3, R1.Pin_1, R2.Pin_1, R3.Pin_1, R4.Pin_1, R5.Pin_1, R6.Pin_1, R7.Pin_1, R8.Pin_1
  N2: Raspberry_Pi1.GPIO4, LED6.cathode
  N3: Raspberry_Pi1.GPIO17, LED1.cathode
  N4: Raspberry_Pi1.GPIO27, LED3.cathode
  N5: Raspberry_Pi1.GPIO22, LED8.cathode
  N6: Raspberry_Pi1.GPIO25, LED7.cathode
  N7: Raspberry_Pi1.GPIO24, LED4.cathode
  N8: Raspberry_Pi1.GPIO23, LED5.cathode
  N9: Raspberry_Pi1.GPIO18, LED2.cathode
  N10: R1.Pin_0, LED1.anode
  N11: LED2.anode, R2.Pin_0
  N12: LED3.anode, R3.Pin_0
  N13: LED4.anode, R7.Pin_0
  N14: LED5.anode, R8.Pin_0
  N15: LED6.anode, R5.Pin_0
  N16: LED7.anode, R6.Pin_0
  N17: LED8.anode, R4.Pin_0
