# Fritzing sketch 08_breathingLed (saved by Fritzing 0.9.2b)
breadboards: 1

parts:
  Raspberry_Pi1 = Raspberry Pi 2
  R1 = Resistor [tolerance=±5% resistance=220 package="2512 [SMD]"]
  LED1 = smd LED [color="Red (633nm)" package="0603 [SMD]"]

nets:
  N1: Raspberry_Pi1.GPIO18, R1.Pin_0
  N2: Raspberry_Pi1.GND, LED1.cathode
  N3: R1.Pin_1, LED1.anode
