# Fritzing sketch 09_rgbLed (saved by Fritzing 0.9.2b)
breadboards: 1

parts:
  Raspberry_Pi1 = Raspberry Pi 2
  R1 = Resistor [tolerance=±5% resistance=220 package="2512 [SMD]"]
  LED2 = RGB LED - (4 legs) [package="5 mm [THT]"]
  R2 = Resistor [tolerance=±5% resistance=220 package="2512 [SMD]"]
  R3 = Resistor [tolerance=±5% resistance=220 package="2512 [SMD]"]

nets:
  N1: Raspberry_Pi1.3v3, LED2.common_anode
  N2: Raspberry_Pi1.GPIO17, R1.Pin_0
  N3: Raspberry_Pi1.GPIO27, R3.Pin_0
  N4: Raspberry_Pi1.GPIO18, R2.Pin_0
  N5: R1.Pin_1, LED2.red_cathode
  N6: LED2.green_cathode, R2.Pin_1
  N7: LED2.blue_cathode, R3.Pin_1
