# Fritzing sketch 10_segment (saved by Fritzing 0.9.2b)
breadboards: 1

parts:
  Raspberry_Pi1 = Raspberry Pi 2
  R1 = Resistor [tolerance=±5% resistance=220 package="2512 [SMD]"]
  DI1 = 7-Segment LED Display [package=THT]

nets:
  N1: Raspberry_Pi1.GPIO4, DI1.cathodeDP
  N2: Raspberry_Pi1.GPIO17, DI1.cathodeA
  N3: Raspberry_Pi1.GPIO27, DI1.cathodeC
  N4: Raspberry_Pi1.GPIO22, DI1.cathodeD
  N5: Raspberry_Pi1.GPIO25, DI1.cathodeG
  N6: Raspberry_Pi1.GPIO24, DI1.cathodeF
  N7: Raspberry_Pi1.GPIO23, DI1.cathodeE
  N8: Raspberry_Pi1.GPIO18, DI1.cathodeB
  N9: Raspberry_Pi1.GND, R1.Pin_0
  N10: R1.Pin_1, DI1.commAnode#2
