# Fritzing sketch 10_segment_595 (saved by Fritzing 0.9.2b)
breadboards: 1

parts:
  Raspberry_Pi1 = Raspberry Pi 2
  R1 = Resistor [tolerance=±5% resistance=220 package="2512 [SMD]"]
  DI1 = 7-Segment LED Display [package=THT]
  U1 = 74HC595 SMD [package="SO16 [SMD]"]

nets:
  N1: Raspberry_Pi1.GPIO17, U1.ST_CP
  N2: Raspberry_Pi1.GPIO27, U1.DS
  N3: Raspberry_Pi1.GPIO18, U1.SH_CP
  GND: Raspberry_Pi1.GND, R1.Pin_0, U1.GND, U1.OE
  5V: Raspberry_Pi1.5V, U1.MR, U1.VCC
  N4: R1.Pin_1, DI1.commAnode#2
  N5: DI1.cathodeE, U1.Q4
  N6: DI1.cathodeD, U1.Q3
  N7: DI1.cathodeC, U1.Q2
  N8: DI1.cathodeDP, U1.Q7
  N9: DI1.cathodeB, U1.Q1
  N10: DI1.cathodeA, U1.Q0
  N11: DI1.cathodeF, U1.Q5
  N12: DI1.cathodeG, U1.Q6
