# Fritzing sketch 12_LCD1602 (saved by Fritzing 0.9.2b)
breadboards: 1

parts:
  Raspberry_Pi1 = Raspberry Pi 2
  LCD1 = LCD screen
  R1 = Rotary Potentiometer (Small) [maximum_resistance=100kΩ package=THT]

nets:
  N1: Raspberry_Pi1.GPIO17, LCD1.DB4
  N2: Raspberry_Pi1.GPIO27, LCD1.DB6
  N3: Raspberry_Pi1.GPIO22, LCD1.DB7
  N4: Raspberry_Pi1.GPIO23, LCD1.E
  N5: Raspberry_Pi1.GPIO18, LCD1.DB5
  GND: Raspberry_Pi1.GND, LCD1.VSS, LCD1.R/W, LCD1.LED-, R1.leg2
  5V: Raspberry_Pi1.5V, LCD1.VDD, LCD1.LED+, R1.leg1
  N6: LCD1.V0, R1.wiper
