# Fritzing sketch 15_dotMartix (saved by Fritzing 0.9.2b)
breadboards: 1

parts:
  Raspberry_Pi1 = Raspberry Pi 2
  U1 = 74HC595 SMD [package="SO16 [SMD]"]
  U2 = 74HC595 SMD [package="SO16 [SMD]"]
  Disp1 = LBT2088AH [part_number=LBT2088AH]

nets:
  N1: Raspberry_Pi1.GPIO17, U1.ST_CP, U2.ST_CP
  N2: Raspberry_Pi1.GPIO27, U2.DS
  N3: Raspberry_Pi1.GPIO18, U1.SH_CP, U2.SH_CP
  GND: Raspberry_Pi1.GND, U1.GND, U1.OE, U2.GND, U2.OE
  VCC: Raspberry_Pi1.5V, U1.MR, U1.VCC, U2.MR, U2.VCC
  N4: U1.Q1, Disp1.pin_14
  N5: U1.Q2, Disp1.pin_8
  N6: U1.Q3, Disp1.pin_12
  N7: U1.Q4, Disp1.pin1
  N8: U1.Q5, Disp1.pin_7
  N9: U1.Q6, Disp1.pin2
  N10: U1.Q7, Disp1.pin_5
  N11: U1.DS, U2.Q7'
  N12: U1.Q0, Disp1.pin_9
  N13: U2.Q1, Disp1.pin_3
  N14: U2.Q2, Disp1.pin_4
  N15: U2.Q3, Disp1.pin_10
  N16: U2.Q4, Disp1.pin_6
  N17: U2.Q5, Disp1.pin_11
  N18: U2.Q6, Disp1.pin_15
  N19: U2.Q7, Disp1.pin_16
  N20: U2.Q0, Disp1.pin_13
