# Fritzing sketch 21_motor (saved by Fritzing 0.9.2b)
breadboards: 1

parts:
  Raspberry_Pi1 = Raspberry Pi 2
  R1 = Resistor [tolerance=±5% resistance=220 package="2512 [SMD]"]
  LED1 = smd LED [color="Red (633nm)" package="0603 [SMD]"]
  U1 = 555 Timer [package="DIP8 [THT]"]
  C1 = Capacitor [package=cap-pth-small2]
  M1 = DC Motor
  S1 = Pushbutton [package="[THT]"]
  S2 = Pushbutton [package="[THT]"]
  S3 = Pushbutton [package="[THT]"]
  S5 = Pushbutton [package="[THT]"]

nets:
  N1: Raspberry_Pi1.3v3, R1.Pin_0
  N2: Raspberry_Pi1.GPIO17, S5.Pin_1, S5.Pin_2
  N3: Raspberry_Pi1.GPIO27, S2.Pin_1, S2.Pin_2
  N4: Raspberry_Pi1.GPIO22, S3.Pin_1, S3.Pin_2
  N5: Raspberry_Pi1.GPIO24, U1.Discharge
  N6: Raspberry_Pi1.GPIO23, U1.Threshold
  N7: Raspberry_Pi1.GPIO18, S1.Pin_1, S1.Pin_2
  N8: Raspberry_Pi1.GPIO15, LED1.cathode
  N9: Raspberry_Pi1.GND, U1.Control_Voltage, U1.Vcc_Supply_Voltage, S1.Pin_3, S1.Pin_4, S2.Pin_3, S2.Pin_4, S3.Pin_3, S3.Pin_4, S5.Pin_3, S5.Pin_4
  N10: R1.Pin_1, LED1.anode
  N11: U1.Ground, C1.2, M1.pin_1
  N12: U1.Trigger, U1.Output
  N13: U1.Reset, C1.1, M1.pin_2
